// Logisim project Zick-Final-Project.circ as structural Verilog
module _16_bit_ALU (
  input  [15:0] A,
  input  [15:0] B,
  input  [1:0] ALU_Op,
  output [15:0] ALU_Out
);

  wire and_1_out;
  wire [15:0] adder_1_out, and_2_out, multiplexer_1_out, not_1_out, or_1_out;

  Multiplexer #(.width(16), .enable("false")) multiplexer_1 (
    .in0(B), .in1(not_1_out), .out(multiplexer_1_out), .sel(and_1_out));
  assign not_1_out = ~B;  // NOT_Gate not_1, 16 bits wide
  and and_1 (and_1_out, ALU_Op[0], ALU_Op[1]);
  Adder #(.width(16)) adder_1 (.a(A), .b(multiplexer_1_out), .out(adder_1_out), .cin(and_1_out));  // open: cout
  assign and_2_out = multiplexer_1_out & A;  // AND_Gate and_2, 16 bits wide
  assign or_1_out = multiplexer_1_out | A;  // OR_Gate or_1, 16 bits wide
  Multiplexer #(.select(2), .width(16), .enable("false")) multiplexer_2 (
    .in0(adder_1_out), .in1(and_2_out), .in2(or_1_out), .in3(adder_1_out), .out(ALU_Out), .sel(ALU_Op));

  // Notes on the sheet:
  //   00 = ADD
  //   01 = AND
  //   10 = OR
  //   11 = SUB
  //   sub not B
  //   sub cin
  //   sub
endmodule

module _16x16_bit_Register_File (
  input  [15:0] Data_In,
  input  Write_Enable,
  input  [3:0] Read_Addr_1,
  input  [3:0] Write_Address,
  input  [3:0] Read_Addr_2,
  input  Clock,
  output [15:0] Read_Data_1,
  output [15:0] Read_Data_2
);

  wire demultiplexer_1_out0, demultiplexer_1_out1, demultiplexer_1_out2, demultiplexer_1_out3,
       demultiplexer_1_out4, demultiplexer_1_out5, demultiplexer_1_out6, demultiplexer_1_out7,
       demultiplexer_1_out8, demultiplexer_1_out9, demultiplexer_1_out10, demultiplexer_1_out11,
       demultiplexer_1_out12, demultiplexer_1_out13, demultiplexer_1_out14, demultiplexer_1_out15;
  wire [15:0] register_1_q, register_2_q, register_3_q, register_4_q, register_5_q, register_6_q,
       register_7_q, register_8_q, register_9_q, register_10_q, register_11_q, register_12_q, register_13_q,
       register_14_q, register_15_q, register_16_q;

  Demultiplexer #(.select(4), .enable("false")) demultiplexer_1 (
    .out0(demultiplexer_1_out0), .out1(demultiplexer_1_out1), .out2(demultiplexer_1_out2),
    .out3(demultiplexer_1_out3), .out4(demultiplexer_1_out4), .out5(demultiplexer_1_out5),
    .out6(demultiplexer_1_out6), .out7(demultiplexer_1_out7), .out8(demultiplexer_1_out8),
    .out9(demultiplexer_1_out9), .out10(demultiplexer_1_out10), .out11(demultiplexer_1_out11),
    .out12(demultiplexer_1_out12), .out13(demultiplexer_1_out13), .out14(demultiplexer_1_out14),
    .out15(demultiplexer_1_out15), .in(Write_Enable), .sel(Write_Address));
  Register #(.width(16)) register_1 (
    .D(Data_In), .en(demultiplexer_1_out0), .Q(register_1_q), .clk(Clock));  // open: clr
  Register #(.width(16)) register_2 (
    .D(Data_In), .en(demultiplexer_1_out1), .Q(register_2_q), .clk(Clock));  // open: clr
  Register #(.width(16)) register_3 (
    .D(Data_In), .en(demultiplexer_1_out2), .Q(register_3_q), .clk(Clock));  // open: clr
  Register #(.width(16)) register_4 (
    .D(Data_In), .en(demultiplexer_1_out3), .Q(register_4_q), .clk(Clock));  // open: clr
  Register #(.width(16)) register_5 (
    .D(Data_In), .en(demultiplexer_1_out4), .Q(register_5_q), .clk(Clock));  // open: clr
  Register #(.width(16)) register_6 (
    .D(Data_In), .en(demultiplexer_1_out5), .Q(register_6_q), .clk(Clock));  // open: clr
  Register #(.width(16)) register_7 (
    .D(Data_In), .en(demultiplexer_1_out6), .Q(register_7_q), .clk(Clock));  // open: clr
  Register #(.width(16)) register_8 (
    .D(Data_In), .en(demultiplexer_1_out7), .Q(register_8_q), .clk(Clock));  // open: clr
  Register #(.width(16)) register_9 (
    .D(Data_In), .en(demultiplexer_1_out8), .Q(register_9_q), .clk(Clock));  // open: clr
  Register #(.width(16)) register_10 (
    .D(Data_In), .en(demultiplexer_1_out9), .Q(register_10_q), .clk(Clock));  // open: clr
  Register #(.width(16)) register_11 (
    .D(Data_In), .en(demultiplexer_1_out10), .Q(register_11_q), .clk(Clock));  // open: clr
  Register #(.width(16)) register_12 (
    .D(Data_In), .en(demultiplexer_1_out11), .Q(register_12_q), .clk(Clock));  // open: clr
  Register #(.width(16)) register_13 (
    .D(Data_In), .en(demultiplexer_1_out12), .Q(register_13_q), .clk(Clock));  // open: clr
  Register #(.width(16)) register_14 (
    .D(Data_In), .en(demultiplexer_1_out13), .Q(register_14_q), .clk(Clock));  // open: clr
  Register #(.width(16)) register_15 (
    .D(Data_In), .en(demultiplexer_1_out14), .Q(register_15_q), .clk(Clock));  // open: clr
  Register #(.width(16)) register_16 (
    .D(Data_In), .en(demultiplexer_1_out15), .Q(register_16_q), .clk(Clock));  // open: clr
  Multiplexer #(.select(4), .width(16), .enable("false")) multiplexer_1 (
    .in0(register_1_q), .in1(register_2_q), .in2(register_3_q), .in3(register_4_q), .in4(register_5_q),
    .in5(register_6_q), .in6(register_7_q), .in7(register_8_q), .in8(register_9_q), .in9(register_10_q),
    .in10(register_11_q), .in11(register_12_q), .in12(register_13_q), .in13(register_14_q),
    .in14(register_15_q), .in15(register_16_q), .out(Read_Data_1), .sel(Read_Addr_1));
  Multiplexer #(.select(4), .width(16), .enable("false")) multiplexer_2 (
    .in0(register_1_q), .in1(register_2_q), .in2(register_3_q), .in3(register_4_q), .in4(register_5_q),
    .in5(register_6_q), .in6(register_7_q), .in7(register_8_q), .in8(register_9_q), .in9(register_10_q),
    .in10(register_11_q), .in11(register_12_q), .in12(register_13_q), .in13(register_14_q),
    .in14(register_15_q), .in15(register_16_q), .out(Read_Data_2), .sel(Read_Addr_2));
endmodule

module _16_bit_ALU_REG_Instruction (
  input  [16:0] CPU_Instruction_Input,
  input  clock,
  output [15:0] CPU_Op_Out
);

  wire [15:0] bit_extender_1_out, multiplexer_1_out, n16x16_bit_register_file_1_read_data_1,
       n16x16_bit_register_file_1_read_data_2;

  _16x16_bit_Register_File u_16x16_bit_register_file_1 (
    .Data_In(CPU_Op_Out), .Write_Enable(1'b1), .Clock(clock), .Write_Address(CPU_Instruction_Input[8:5]),
    .Read_Addr_1(CPU_Instruction_Input[12:9]), .Read_Addr_2(CPU_Instruction_Input[16:13]),
    .Read_Data_1(n16x16_bit_register_file_1_read_data_1), .Read_Data_2(n16x16_bit_register_file_1_read_data_2));
  assign bit_extender_1_out = {{12{CPU_Instruction_Input[16]}}, CPU_Instruction_Input[16:13]};  // Bit_Extender bit_extender_1
  Multiplexer #(.width(16), .enable("false")) multiplexer_1 (
    .in0(n16x16_bit_register_file_1_read_data_2), .in1(bit_extender_1_out), .out(multiplexer_1_out),
    .sel(CPU_Instruction_Input[4]));
  _16_bit_ALU u_16_bit_alu_1 (
    .A(n16x16_bit_register_file_1_read_data_1), .B(multiplexer_1_out), .ALU_Op(CPU_Instruction_Input[1:0]),
    .ALU_Out(CPU_Op_Out));

  // Notes on the sheet:
  //   op code
  //   src2
  //   ALU op
  //   dest
  //   src1
  //   immed data
  //   immed select
endmodule

module _16_bit_ALU_with_Memory (
  input  [16:0] CPU_Instruction_Input,
  input  clock,
  output [15:0] CPU_Op_Out
);

  wire basic_control_logic_lookup_table_1_immediate_select, basic_control_logic_lookup_table_1_load_word,
       basic_control_logic_lookup_table_1_register_write_enable,
       basic_control_logic_lookup_table_1_store_word, or_1_out;
  wire [1:0] basic_control_logic_lookup_table_1_alu_op_code;
  wire [15:0] bit_extender_1_out, multiplexer_1_out, multiplexer_2_out,
       n16x16_bit_register_file_1_read_data_1, n16x16_bit_register_file_1_read_data_2, ram_1_data;

  Basic_Control_Logic_Lookup_Table basic_control_logic_lookup_table_1 (
    .Opcode(CPU_Instruction_Input[4:0]),
    .Register_Write_Enable(basic_control_logic_lookup_table_1_register_write_enable),
    .Immediate_Select(basic_control_logic_lookup_table_1_immediate_select),
    .Store_Word(basic_control_logic_lookup_table_1_store_word),
    .Load_Word(basic_control_logic_lookup_table_1_load_word),
    .ALU_OP_Code(basic_control_logic_lookup_table_1_alu_op_code));
  assign bit_extender_1_out = {{12{CPU_Instruction_Input[16]}}, CPU_Instruction_Input[16:13]};  // Bit_Extender bit_extender_1
  _16x16_bit_Register_File u_16x16_bit_register_file_1 (
    .Data_In(CPU_Op_Out), .Write_Enable(basic_control_logic_lookup_table_1_register_write_enable),
    .Clock(clock), .Write_Address(CPU_Instruction_Input[8:5]), .Read_Addr_1(CPU_Instruction_Input[12:9]),
    .Read_Addr_2(CPU_Instruction_Input[16:13]), .Read_Data_1(n16x16_bit_register_file_1_read_data_1),
    .Read_Data_2(n16x16_bit_register_file_1_read_data_2));
  Multiplexer #(.width(16), .enable("false")) multiplexer_1 (
    .in0(n16x16_bit_register_file_1_read_data_2), .in1(bit_extender_1_out), .out(multiplexer_1_out),
    .sel(basic_control_logic_lookup_table_1_immediate_select));
  _16_bit_ALU u_16_bit_alu_1 (
    .A(n16x16_bit_register_file_1_read_data_1), .B(multiplexer_1_out),
    .ALU_Op(basic_control_logic_lookup_table_1_alu_op_code), .ALU_Out(CPU_Op_Out));
  Multiplexer #(.width(16), .enable("false")) multiplexer_2 (
    .in0(ram_1_data), .in1(CPU_Op_Out), .out(multiplexer_2_out),
    .sel(basic_control_logic_lookup_table_1_load_word));
  or or_1 (or_1_out, basic_control_logic_lookup_table_1_store_word, basic_control_logic_lookup_table_1_load_word);
  RAM #(.addrWidth(16), .dataWidth(16), .bus("separate")) ram_1 (
    .addr(CPU_Op_Out), .din(multiplexer_2_out), .data(ram_1_data),
    .str(basic_control_logic_lookup_table_1_store_word), .sel(or_1_out), .clk(clock),
    .ld(basic_control_logic_lookup_table_1_load_word));  // open: clr

  // Notes on the sheet:
  //   op code
  //   src1
  //   src2
  //   immed data
  //   immed select
  //   ALU op
  //   dest
endmodule

module Basic_Control_Logic_Lookup_Table (
  input  [4:0] Opcode,
  output Register_Write_Enable,
  output Immediate_Select,
  output Store_Word,
  output Load_Word,
  output [1:0] ALU_OP_Code
);

  wire [1:0] ram_1_data;

  RAM #(.addrWidth(5), .bus("separate")) ram_1 (
    .addr(Opcode),
    .data({Register_Write_Enable, Immediate_Select, Store_Word, Load_Word, ALU_OP_Code, ram_1_data}),
    .ld(1'b1));  // open: din, str, sel, clk, clr
  // Probe on {Register_Write_Enable, Immediate_Select, Store_Word, Load_Word, ALU_OP_Code, ram_1_data}

  // Notes on the sheet:
  //   Bit 2 is Store Word
  //   Bit 3 is Load Word
  //   Bit 0 is Register Write Enable
  //   Bit 1 is Immediate Select
  //   Bits 4 and 5 are ALU OP Code
endmodule

module Full_16_bit_CPU (
  input  [16:0] CPU_Instruction_Input,
  input  clock,
  output [15:0] CPU_Op_Out
);

  wire basic_control_logic_lookup_table_1_immediate_select, basic_control_logic_lookup_table_1_load_word,
       basic_control_logic_lookup_table_1_register_write_enable,
       basic_control_logic_lookup_table_1_store_word, or_1_out;
  wire [1:0] basic_control_logic_lookup_table_1_alu_op_code;
  wire [15:0] bit_extender_1_out, multiplexer_1_out, multiplexer_2_out,
       n16x16_bit_register_file_1_read_data_1, n16x16_bit_register_file_1_read_data_2, ram_2_data;
  wire [16:0] adder_1_out, ram_1_data, register_1_q;

  Adder #(.width(17)) adder_1 (.a(17'h1), .b(register_1_q), .out(adder_1_out));  // open: cin, cout
  Register #(.width(17)) register_1 (.D(adder_1_out), .Q(register_1_q), .clk(clock));  // open: en, clr
  // Probe on ram_1_data
  RAM #(.addrWidth(17), .dataWidth(17), .bus("separate")) ram_1 (
    .addr(register_1_q), .data(ram_1_data), .clk(clock));  // open: din, str, sel, ld, clr
  // Probe on ram_1_data[16:12]
  Basic_Control_Logic_Lookup_Table basic_control_logic_lookup_table_1 (
    .Opcode(ram_1_data[16:12]),
    .Register_Write_Enable(basic_control_logic_lookup_table_1_register_write_enable),
    .Immediate_Select(basic_control_logic_lookup_table_1_immediate_select),
    .Store_Word(basic_control_logic_lookup_table_1_store_word),
    .Load_Word(basic_control_logic_lookup_table_1_load_word),
    .ALU_OP_Code(basic_control_logic_lookup_table_1_alu_op_code));
  // Probe on basic_control_logic_lookup_table_1_alu_op_code
  // Probe on ram_1_data[11:8]
  // Probe on ram_1_data[7:4]
  // Probe on ram_1_data[3:0]
  _16x16_bit_Register_File u_16x16_bit_register_file_1 (
    .Data_In(CPU_Op_Out), .Write_Enable(basic_control_logic_lookup_table_1_register_write_enable),
    .Clock(clock), .Write_Address(ram_1_data[11:8]), .Read_Addr_1(ram_1_data[7:4]),
    .Read_Addr_2(ram_1_data[3:0]), .Read_Data_1(n16x16_bit_register_file_1_read_data_1),
    .Read_Data_2(n16x16_bit_register_file_1_read_data_2));
  assign bit_extender_1_out = {{12{ram_1_data[3]}}, ram_1_data[3:0]};  // Bit_Extender bit_extender_1
  _16_bit_ALU u_16_bit_alu_1 (
    .A(n16x16_bit_register_file_1_read_data_1), .B(multiplexer_1_out),
    .ALU_Op(basic_control_logic_lookup_table_1_alu_op_code), .ALU_Out(CPU_Op_Out));
  Multiplexer #(.width(16), .enable("false")) multiplexer_1 (
    .in0(n16x16_bit_register_file_1_read_data_2), .in1(bit_extender_1_out), .out(multiplexer_1_out),
    .sel(basic_control_logic_lookup_table_1_immediate_select));
  // Probe on ram_2_data
  Multiplexer #(.width(16), .enable("false")) multiplexer_2 (
    .in0(CPU_Op_Out), .in1(ram_2_data), .out(multiplexer_2_out),
    .sel(basic_control_logic_lookup_table_1_load_word));
  or or_1 (or_1_out, basic_control_logic_lookup_table_1_store_word, basic_control_logic_lookup_table_1_load_word);
  RAM #(.addrWidth(16), .dataWidth(16), .bus("separate")) ram_2 (
    .addr(CPU_Op_Out), .din(multiplexer_2_out), .data(ram_2_data),
    .str(basic_control_logic_lookup_table_1_store_word), .sel(or_1_out), .clk(clock),
    .ld(basic_control_logic_lookup_table_1_load_word));  // open: clr

  // Notes on the sheet:
  //   op code
  //   src2
  //   src1
  //   immed data
  //   immed select
  //   ALU op
  //   dest
endmodule

module _4_bit_CLA_block (
  input  C_in,
  input  [3:0] A,
  input  [3:0] B,
  output [3:0] S,
  output C_out
);

  wire adder_1_cout, adder_2_cout, adder_3_cout, and_1_out, and_2_out, and_3_out, and_4_out, and_5_out,
       G0_out, G1_out, G2_out, G3_out, or_1_out, or_2_out, or_3_out, P0_out, P1_out, P2_out, P3_out;

  or P2 (P2_out, B[2], A[2]);
  or P3 (P3_out, B[3], A[3]);
  or P1 (P1_out, B[1], A[1]);
  and G3 (G3_out, B[3], A[3]);
  or P0 (P0_out, B[0], A[0]);
  and G2 (G2_out, B[2], A[2]);
  and G1 (G1_out, B[1], A[1]);
  and G0 (G0_out, B[0], A[0]);
  Adder #(.width(1)) adder_1 (.a(A[0]), .b(B[0]), .out(S[0]), .cin(C_in), .cout(adder_1_cout));
  Adder #(.width(1)) adder_2 (.a(A[1]), .b(B[1]), .out(S[1]), .cin(adder_1_cout), .cout(adder_2_cout));
  Adder #(.width(1)) adder_3 (.a(A[2]), .b(B[2]), .out(S[2]), .cin(adder_2_cout), .cout(adder_3_cout));
  Adder #(.width(1)) adder_4 (.a(A[3]), .b(B[3]), .out(S[3]), .cin(adder_3_cout));  // open: cout
  and and_1 (and_1_out, G0_out, P1_out);
  or or_1 (or_1_out, and_1_out, G1_out);
  and and_2 (and_2_out, or_1_out, P2_out);
  or or_2 (or_2_out, and_2_out, G2_out);
  and and_3 (and_3_out, or_2_out, P3_out);
  and and_4 (and_4_out, P0_out, P1_out, P2_out, P3_out);
  or or_3 (or_3_out, and_3_out, G3_out);
  and and_5 (and_5_out, C_in, and_4_out);
  or or_4 (C_out, or_3_out, and_5_out);
endmodule

module _16_bit_CLA_Adder (
  input  C_in,
  input  [15:0] A,
  input  [15:0] B,
  output [15:0] S,
  output C_out
);

  wire n4_bit_cla_block_1_c_out, n4_bit_cla_block_2_c_out, n4_bit_cla_block_3_c_out;

  _4_bit_CLA_block u_4_bit_cla_block_1 (
    .C_in(C_in), .A(A[3:0]), .B(B[3:0]), .S(S[3:0]), .C_out(n4_bit_cla_block_1_c_out));
  _4_bit_CLA_block u_4_bit_cla_block_2 (
    .C_in(n4_bit_cla_block_1_c_out), .A(A[7:4]), .B(B[7:4]), .S(S[7:4]), .C_out(n4_bit_cla_block_2_c_out));
  _4_bit_CLA_block u_4_bit_cla_block_3 (
    .C_in(n4_bit_cla_block_2_c_out), .A(A[11:8]), .B(B[11:8]), .S(S[11:8]), .C_out(n4_bit_cla_block_3_c_out));
  _4_bit_CLA_block u_4_bit_cla_block_4 (
    .C_in(n4_bit_cla_block_3_c_out), .A(A[15:12]), .B(B[15:12]), .S(S[15:12]), .C_out(C_out));
endmodule

module _16_bit_CLA_ALU (
  input  [15:0] A,
  input  [15:0] B,
  input  [1:0] ALU_Op,
  output [15:0] ALU_Out
);

  wire and_1_out;
  wire [15:0] and_2_out, multiplexer_1_out, n16_bit_cla_adder_1_s, not_1_out, or_1_out;

  Multiplexer #(.width(16), .enable("false")) multiplexer_1 (
    .in0(B), .in1(not_1_out), .out(multiplexer_1_out), .sel(and_1_out));
  assign not_1_out = ~B;  // NOT_Gate not_1, 16 bits wide
  and and_1 (and_1_out, ALU_Op[0], ALU_Op[1]);
  _16_bit_CLA_Adder u_16_bit_cla_adder_1 (
    .A(A), .B(multiplexer_1_out), .C_in(and_1_out), .S(n16_bit_cla_adder_1_s));  // open: C_out
  assign and_2_out = multiplexer_1_out & A;  // AND_Gate and_2, 16 bits wide
  assign or_1_out = multiplexer_1_out | A;  // OR_Gate or_1, 16 bits wide
  Multiplexer #(.select(2), .width(16), .enable("false")) multiplexer_2 (
    .in0(n16_bit_cla_adder_1_s), .in1(and_2_out), .in2(or_1_out), .in3(n16_bit_cla_adder_1_s), .out(ALU_Out),
    .sel(ALU_Op));

  // Notes on the sheet:
  //   00 = ADD
  //   01 = AND
  //   10 = OR
  //   11 = SUB
  //   sub not B
  //   sub cin
  //   sub
endmodule

module Full_16_bit_CPU_with_CLA (
  input  [16:0] CPU_Instruction_Input,
  input  clock,
  output [15:0] CPU_Op_Out
);

  wire basic_control_logic_lookup_table_1_immediate_select, basic_control_logic_lookup_table_1_load_word,
       basic_control_logic_lookup_table_1_register_write_enable,
       basic_control_logic_lookup_table_1_store_word, or_1_out;
  wire [1:0] basic_control_logic_lookup_table_1_alu_op_code;
  wire [15:0] bit_extender_1_out, multiplexer_1_out, multiplexer_2_out,
       n16x16_bit_register_file_1_read_data_1, n16x16_bit_register_file_1_read_data_2, ram_2_data;
  wire [16:0] adder_1_out, ram_1_data, register_1_q;

  Adder #(.width(17)) adder_1 (.a(17'h1), .b(register_1_q), .out(adder_1_out));  // open: cin, cout
  Register #(.width(17)) register_1 (.D(adder_1_out), .Q(register_1_q), .clk(clock));  // open: en, clr
  // Probe on ram_1_data
  RAM #(.addrWidth(17), .dataWidth(17), .bus("separate")) ram_1 (
    .addr(register_1_q), .data(ram_1_data), .clk(clock));  // open: din, str, sel, ld, clr
  Basic_Control_Logic_Lookup_Table basic_control_logic_lookup_table_1 (
    .Opcode(ram_1_data[16:12]),
    .Register_Write_Enable(basic_control_logic_lookup_table_1_register_write_enable),
    .Immediate_Select(basic_control_logic_lookup_table_1_immediate_select),
    .Store_Word(basic_control_logic_lookup_table_1_store_word),
    .Load_Word(basic_control_logic_lookup_table_1_load_word),
    .ALU_OP_Code(basic_control_logic_lookup_table_1_alu_op_code));
  // Probe on basic_control_logic_lookup_table_1_alu_op_code
  // Probe on ram_1_data[16:12]
  // Probe on ram_1_data[11:8]
  // Probe on ram_1_data[7:4]
  // Probe on ram_1_data[3:0]
  _16x16_bit_Register_File u_16x16_bit_register_file_1 (
    .Data_In(CPU_Op_Out), .Write_Enable(basic_control_logic_lookup_table_1_register_write_enable),
    .Clock(clock), .Write_Address(ram_1_data[11:8]), .Read_Addr_1(ram_1_data[7:4]),
    .Read_Addr_2(ram_1_data[3:0]), .Read_Data_1(n16x16_bit_register_file_1_read_data_1),
    .Read_Data_2(n16x16_bit_register_file_1_read_data_2));
  Multiplexer #(.width(16), .enable("false")) multiplexer_1 (
    .in0(n16x16_bit_register_file_1_read_data_2), .in1(bit_extender_1_out), .out(multiplexer_1_out),
    .sel(basic_control_logic_lookup_table_1_immediate_select));
  assign bit_extender_1_out = {{12{ram_1_data[3]}}, ram_1_data[3:0]};  // Bit_Extender bit_extender_1
  _16_bit_CLA_ALU u_16_bit_cla_alu_1 (
    .A(n16x16_bit_register_file_1_read_data_1), .B(multiplexer_1_out),
    .ALU_Op(basic_control_logic_lookup_table_1_alu_op_code), .ALU_Out(CPU_Op_Out));
  // Probe on ram_2_data
  Multiplexer #(.width(16), .enable("false")) multiplexer_2 (
    .in0(CPU_Op_Out), .in1(ram_2_data), .out(multiplexer_2_out),
    .sel(basic_control_logic_lookup_table_1_load_word));
  or or_1 (or_1_out, basic_control_logic_lookup_table_1_store_word, basic_control_logic_lookup_table_1_load_word);
  RAM #(.addrWidth(16), .dataWidth(16), .bus("separate")) ram_2 (
    .addr(CPU_Op_Out), .din(multiplexer_2_out), .data(ram_2_data),
    .str(basic_control_logic_lookup_table_1_store_word), .sel(or_1_out), .clk(clock),
    .ld(basic_control_logic_lookup_table_1_load_word));  // open: clr

  // Notes on the sheet:
  //   op code
  //   src2
  //   immed data
  //   immed select
  //   ALU op
  //   dest
  //   src1
endmodule

module Full_CPU_with_Branches (
  input  [16:0] CPU_Instruction_Input,
  input  clock,
  output [15:0] CPU_Op_Out
);

  wire and_1_out, kitchen_sink_control_logic_lookup_table_1_branch,
       kitchen_sink_control_logic_lookup_table_1_immediate_select,
       kitchen_sink_control_logic_lookup_table_1_jump, kitchen_sink_control_logic_lookup_table_1_load_word,
       kitchen_sink_control_logic_lookup_table_1_register_write_enable,
       kitchen_sink_control_logic_lookup_table_1_store_word, n16_bit_cla_alu_with_zero_1_zero, or_1_out;
  wire [1:0] kitchen_sink_control_logic_lookup_table_1_alu_op_code;
  wire [15:0] bit_extender_1_out, multiplexer_2_out, multiplexer_3_out,
       n16x16_bit_register_file_1_read_data_1, n16x16_bit_register_file_1_read_data_2, ram_2_data;
  wire [16:0] adder_1_out, adder_2_out, bit_extender_2_out, multiplexer_1_out, ram_1_data, register_1_q;

  // Probe on bit_extender_2_out
  and and_1 (and_1_out, n16_bit_cla_alu_with_zero_1_zero, kitchen_sink_control_logic_lookup_table_1_branch);
  Multiplexer #(.width(17), .enable("false")) multiplexer_1 (
    .in0(adder_2_out), .in1(adder_1_out), .out(multiplexer_1_out), .sel(and_1_out));
  Adder #(.width(17)) adder_1 (.a(adder_2_out), .b(bit_extender_2_out), .out(adder_1_out));  // open: cin, cout
  Adder #(.width(17)) adder_2 (.a(17'h1), .b(register_1_q), .out(adder_2_out));  // open: cin, cout
  Register #(.width(17)) register_1 (.D(multiplexer_1_out), .Q(register_1_q), .clk(clock));  // open: en, clr
  // Probe on adder_1_out
  // Probe on ram_1_data
  RAM #(.addrWidth(17), .dataWidth(17), .bus("separate")) ram_1 (
    .addr(register_1_q), .data(ram_1_data), .str(1'b0), .clk(clock));  // open: din, sel, ld, clr
  Kitchen_Sink_Control_Logic_Lookup_Table kitchen_sink_control_logic_lookup_table_1 (
    .Opcode(ram_1_data[16:12]),
    .Register_Write_Enable(kitchen_sink_control_logic_lookup_table_1_register_write_enable),
    .Immediate_Select(kitchen_sink_control_logic_lookup_table_1_immediate_select),
    .Store_Word(kitchen_sink_control_logic_lookup_table_1_store_word),
    .Load_Word(kitchen_sink_control_logic_lookup_table_1_load_word),
    .ALU_OP_Code(kitchen_sink_control_logic_lookup_table_1_alu_op_code),
    .Jump(kitchen_sink_control_logic_lookup_table_1_jump),
    .Branch(kitchen_sink_control_logic_lookup_table_1_branch));
  // Probe on ram_1_data[16:12]
  // Probe on kitchen_sink_control_logic_lookup_table_1_alu_op_code
  // Probe on ram_1_data[11:8]
  // Probe on ram_1_data[7:4]
  // Probe on ram_1_data[3:0]
  _16x16_bit_Register_File u_16x16_bit_register_file_1 (
    .Data_In(CPU_Op_Out), .Write_Enable(kitchen_sink_control_logic_lookup_table_1_register_write_enable),
    .Clock(clock), .Write_Address(ram_1_data[11:8]), .Read_Addr_1(ram_1_data[7:4]),
    .Read_Addr_2(ram_1_data[3:0]), .Read_Data_1(n16x16_bit_register_file_1_read_data_1),
    .Read_Data_2(n16x16_bit_register_file_1_read_data_2));
  Multiplexer #(.width(16), .enable("false")) multiplexer_2 (
    .in0(n16x16_bit_register_file_1_read_data_2), .in1(bit_extender_1_out), .out(multiplexer_2_out),
    .sel(kitchen_sink_control_logic_lookup_table_1_immediate_select));
  assign bit_extender_1_out = {{12{ram_1_data[3]}}, ram_1_data[3:0]};  // Bit_Extender bit_extender_1
  assign bit_extender_2_out = {{13{ram_1_data[11]}}, ram_1_data[11:8]};  // Bit_Extender bit_extender_2
  _16_bit_CLA_ALU_with_Zero u_16_bit_cla_alu_with_zero_1 (
    .A(n16x16_bit_register_file_1_read_data_1), .B(multiplexer_2_out),
    .ALU_Op(kitchen_sink_control_logic_lookup_table_1_alu_op_code), .ALU_Out(CPU_Op_Out),
    .Zero(n16_bit_cla_alu_with_zero_1_zero));
  // Probe on ram_2_data
  Multiplexer #(.width(16), .enable("false")) multiplexer_3 (
    .in0(CPU_Op_Out), .in1(ram_2_data), .out(multiplexer_3_out),
    .sel(kitchen_sink_control_logic_lookup_table_1_load_word));
  or or_1 (or_1_out, kitchen_sink_control_logic_lookup_table_1_store_word, kitchen_sink_control_logic_lookup_table_1_load_word);
  RAM #(.addrWidth(16), .dataWidth(16), .bus("separate")) ram_2 (
    .addr(CPU_Op_Out), .din(multiplexer_3_out), .data(ram_2_data),
    .str(kitchen_sink_control_logic_lookup_table_1_store_word), .sel(or_1_out), .clk(clock),
    .ld(kitchen_sink_control_logic_lookup_table_1_load_word));  // open: clr

  // Notes on the sheet:
  //   branch
  //   op code
  //   branch
  //   src2
  //   immed data
  //   immed select
  //   ALU op
  //   dest
  //   src1
  //   jump
  //   store word
  //   load word
endmodule

module Full_CPU_with_Jumps (
  input  [16:0] CPU_Instruction_Input,
  input  clock,
  output [15:0] CPU_Op_Out
);

  wire and_1_out, kitchen_sink_control_logic_lookup_table_1_branch,
       kitchen_sink_control_logic_lookup_table_1_immediate_select,
       kitchen_sink_control_logic_lookup_table_1_jump, kitchen_sink_control_logic_lookup_table_1_load_word,
       kitchen_sink_control_logic_lookup_table_1_register_write_enable,
       kitchen_sink_control_logic_lookup_table_1_store_word, n16_bit_cla_alu_with_zero_1_zero, or_1_out;
  wire [1:0] kitchen_sink_control_logic_lookup_table_1_alu_op_code;
  wire [4:0] ram_1_data_2;
  wire [11:0] ram_1_data;
  wire [15:0] bit_extender_1_out, multiplexer_3_out, multiplexer_4_out,
       n16x16_bit_register_file_1_read_data_1, n16x16_bit_register_file_1_read_data_2, ram_2_data;
  wire [16:0] adder_1_out, adder_2_out, bit_extender_2_out, multiplexer_1_out, multiplexer_2_out,
       register_1_q;

  // Probe on bit_extender_2_out
  and and_1 (and_1_out, n16_bit_cla_alu_with_zero_1_zero, kitchen_sink_control_logic_lookup_table_1_branch);
  Multiplexer #(.width(17), .enable("false")) multiplexer_1 (
    .in0(adder_2_out), .in1(adder_1_out), .out(multiplexer_1_out), .sel(and_1_out));
  Adder #(.width(17)) adder_1 (.a(adder_2_out), .b(bit_extender_2_out), .out(adder_1_out));  // open: cin, cout
  // Probe on {adder_2_out[16:12], ram_1_data}
  Adder #(.width(17)) adder_2 (.a(17'h1), .b(register_1_q), .out(adder_2_out));  // open: cin, cout
  Register #(.width(17)) register_1 (.D(multiplexer_2_out), .Q(register_1_q), .clk(clock));  // open: en, clr
  Multiplexer #(.width(17), .enable("false")) multiplexer_2 (
    .in0(multiplexer_1_out), .in1({adder_2_out[16:12], ram_1_data}), .out(multiplexer_2_out),
    .sel(kitchen_sink_control_logic_lookup_table_1_jump));
  // Probe on adder_2_out
  // Probe on adder_1_out
  // Probe on {ram_1_data_2, ram_1_data}
  // Probe on {ram_1_data_2, ram_1_data}
  RAM #(.addrWidth(17), .dataWidth(17), .bus("separate")) ram_1 (
    .addr(register_1_q), .data({ram_1_data_2, ram_1_data}), .str(1'b0), .clk(clock));  // open: din, sel, ld, clr
  Kitchen_Sink_Control_Logic_Lookup_Table kitchen_sink_control_logic_lookup_table_1 (
    .Opcode(ram_1_data_2),
    .Register_Write_Enable(kitchen_sink_control_logic_lookup_table_1_register_write_enable),
    .Immediate_Select(kitchen_sink_control_logic_lookup_table_1_immediate_select),
    .Store_Word(kitchen_sink_control_logic_lookup_table_1_store_word),
    .Load_Word(kitchen_sink_control_logic_lookup_table_1_load_word),
    .ALU_OP_Code(kitchen_sink_control_logic_lookup_table_1_alu_op_code),
    .Jump(kitchen_sink_control_logic_lookup_table_1_jump),
    .Branch(kitchen_sink_control_logic_lookup_table_1_branch));
  // Probe on ram_1_data_2
  // Probe on kitchen_sink_control_logic_lookup_table_1_alu_op_code
  // Probe on ram_1_data[11:8]
  // Probe on ram_1_data[7:4]
  // Probe on ram_1_data[3:0]
  _16x16_bit_Register_File u_16x16_bit_register_file_1 (
    .Data_In(CPU_Op_Out), .Write_Enable(kitchen_sink_control_logic_lookup_table_1_register_write_enable),
    .Clock(clock), .Write_Address(ram_1_data[11:8]), .Read_Addr_1(ram_1_data[7:4]),
    .Read_Addr_2(ram_1_data[3:0]), .Read_Data_1(n16x16_bit_register_file_1_read_data_1),
    .Read_Data_2(n16x16_bit_register_file_1_read_data_2));
  Multiplexer #(.width(16), .enable("false")) multiplexer_3 (
    .in0(n16x16_bit_register_file_1_read_data_2), .in1(bit_extender_1_out), .out(multiplexer_3_out),
    .sel(kitchen_sink_control_logic_lookup_table_1_immediate_select));
  assign bit_extender_1_out = {{12{ram_1_data[3]}}, ram_1_data[3:0]};  // Bit_Extender bit_extender_1
  assign bit_extender_2_out = {{13{ram_1_data[11]}}, ram_1_data[11:8]};  // Bit_Extender bit_extender_2
  _16_bit_CLA_ALU_with_Zero u_16_bit_cla_alu_with_zero_1 (
    .A(n16x16_bit_register_file_1_read_data_1), .B(multiplexer_3_out),
    .ALU_Op(kitchen_sink_control_logic_lookup_table_1_alu_op_code), .ALU_Out(CPU_Op_Out),
    .Zero(n16_bit_cla_alu_with_zero_1_zero));
  // Probe on ram_2_data
  Multiplexer #(.width(16), .enable("false")) multiplexer_4 (
    .in0(CPU_Op_Out), .in1(ram_2_data), .out(multiplexer_4_out),
    .sel(kitchen_sink_control_logic_lookup_table_1_load_word));
  or or_1 (or_1_out, kitchen_sink_control_logic_lookup_table_1_store_word, kitchen_sink_control_logic_lookup_table_1_load_word);
  RAM #(.addrWidth(16), .dataWidth(16), .bus("separate")) ram_2 (
    .addr(CPU_Op_Out), .din(multiplexer_4_out), .data(ram_2_data),
    .str(kitchen_sink_control_logic_lookup_table_1_store_word), .sel(or_1_out), .clk(clock),
    .ld(kitchen_sink_control_logic_lookup_table_1_load_word));  // open: clr

  // Notes on the sheet:
  //   branch
  //   op code
  //   branch
  //   src2
  //   immed data
  //   immed select
  //   ALU op
  //   dest
  //   src1
  //   jump
  //   store word
  //   load word
endmodule

module _16_bit_CLA_ALU_with_Zero (
  input  [15:0] A,
  input  [15:0] B,
  input  [1:0] ALU_Op,
  output [15:0] ALU_Out,
  output Zero
);

  wire and_1_out;
  wire [15:0] and_2_out, multiplexer_1_out, n16_bit_cla_adder_1_s, not_1_out, or_1_out;

  Multiplexer #(.width(16), .enable("false")) multiplexer_1 (
    .in0(B), .in1(not_1_out), .out(multiplexer_1_out), .sel(and_1_out));
  assign not_1_out = ~B;  // NOT_Gate not_1, 16 bits wide
  and and_1 (and_1_out, ALU_Op[0], ALU_Op[1]);
  _16_bit_CLA_Adder u_16_bit_cla_adder_1 (
    .A(A), .B(multiplexer_1_out), .C_in(and_1_out), .S(n16_bit_cla_adder_1_s));  // open: C_out
  assign and_2_out = multiplexer_1_out & A;  // AND_Gate and_2, 16 bits wide
  assign or_1_out = multiplexer_1_out | A;  // OR_Gate or_1, 16 bits wide
  Multiplexer #(.select(2), .width(16), .enable("false")) multiplexer_2 (
    .in0(n16_bit_cla_adder_1_s), .in1(and_2_out), .in2(or_1_out), .in3(n16_bit_cla_adder_1_s), .out(ALU_Out),
    .sel(ALU_Op));
  Comparator #(.width(16)) comparator_1 (.a(ALU_Out), .b({16{1'b0}}), .eq(Zero));  // open: gt, lt
  Pull_Resistor pull_resistor_1 (.node(Zero));

  // Notes on the sheet:
  //   Zero: pull=down
  //   00 = ADD
  //   01 = AND
  //   10 = OR
  //   11 = SUB
  //   sub not B
  //   sub cin
  //   sub
endmodule

module Kitchen_Sink_Control_Logic_Lookup_Table (
  input  [4:0] Opcode,
  output Register_Write_Enable,
  output Immediate_Select,
  output Store_Word,
  output Load_Word,
  output [1:0] ALU_OP_Code,
  output Jump,
  output Branch
);

  RAM #(.addrWidth(5), .bus("separate")) ram_1 (
    .addr(Opcode),
    .data({Register_Write_Enable, Immediate_Select, Store_Word, Load_Word, ALU_OP_Code, Jump, Branch}),
    .ld(1'b1));  // open: din, str, sel, clk, clr
  // Probe on {Register_Write_Enable, Immediate_Select, Store_Word, Load_Word, ALU_OP_Code, Jump, Branch}

  // Notes on the sheet:
  //   Bit 1 is Jump
  //   Bit 0 is Branch
  //   Bit 7 is Register Enable
  //   Bit 6 is Immediate Select
  //   Bit 5 is Store Word
  //   Bit 4 is Load Word
  //   Bits 3 and 2 are ALU OP Code
endmodule

module Full_CPU_with_SLT_SGT (
  input  [16:0] CPU_Instruction_Input,
  input  clock,
  input  Clear,
  output [15:0] CPU_Op_Out
);

  wire and_1_out, kitchen_sink_control_logic_with_3_alu_bits_1_branch,
       kitchen_sink_control_logic_with_3_alu_bits_1_immediate_select,
       kitchen_sink_control_logic_with_3_alu_bits_1_jump,
       kitchen_sink_control_logic_with_3_alu_bits_1_load_word,
       kitchen_sink_control_logic_with_3_alu_bits_1_register_write_enable,
       kitchen_sink_control_logic_with_3_alu_bits_1_store_word, n16_bit_cla_alu_with_comparator_1_zero,
       or_1_out;
  wire [2:0] kitchen_sink_control_logic_with_3_alu_bits_1_alu_op_code;
  wire [4:0] ram_1_data_2;
  wire [11:0] ram_1_data;
  wire [15:0] bit_extender_1_out, multiplexer_3_out, multiplexer_4_out,
       n16x16_bit_register_file_with_clear_1_read_data_1, n16x16_bit_register_file_with_clear_1_read_data_2,
       ram_2_data;
  wire [16:0] adder_1_out, adder_2_out, bit_extender_2_out, multiplexer_1_out, multiplexer_2_out,
       register_1_q;

  // Probe on bit_extender_2_out
  and and_1 (and_1_out, n16_bit_cla_alu_with_comparator_1_zero, kitchen_sink_control_logic_with_3_alu_bits_1_branch);
  Multiplexer #(.width(17), .enable("false")) multiplexer_1 (
    .in0(adder_2_out), .in1(adder_1_out), .out(multiplexer_1_out), .sel(and_1_out));
  Adder #(.width(17)) adder_1 (.a(adder_2_out), .b(bit_extender_2_out), .out(adder_1_out));  // open: cin, cout
  // Probe on {adder_2_out[16:12], ram_1_data}
  Adder #(.width(17)) adder_2 (.a(17'h1), .b(register_1_q), .out(adder_2_out));  // open: cin, cout
  Multiplexer #(.width(17), .enable("false")) multiplexer_2 (
    .in0(multiplexer_1_out), .in1({adder_2_out[16:12], ram_1_data}), .out(multiplexer_2_out),
    .sel(kitchen_sink_control_logic_with_3_alu_bits_1_jump));
  Register #(.width(17)) register_1 (.D(multiplexer_2_out), .Q(register_1_q), .clk(clock), .clr(Clear));  // open: en
  // Probe on adder_2_out
  // Probe on adder_1_out
  // Probe on {ram_1_data_2, ram_1_data}
  // Probe on {ram_1_data_2, ram_1_data}
  RAM #(.addrWidth(17), .dataWidth(17), .bus("separate")) ram_1 (
    .addr(register_1_q), .data({ram_1_data_2, ram_1_data}), .str(1'b0), .clk(clock), .clr(Clear));  // open: din, sel, ld
  Kitchen_Sink_Control_Logic_with_3_ALU_bits kitchen_sink_control_logic_with_3_alu_bits_1 (
    .Opcode(ram_1_data_2),
    .Register_Write_Enable(kitchen_sink_control_logic_with_3_alu_bits_1_register_write_enable),
    .Immediate_Select(kitchen_sink_control_logic_with_3_alu_bits_1_immediate_select),
    .Store_Word(kitchen_sink_control_logic_with_3_alu_bits_1_store_word),
    .Load_Word(kitchen_sink_control_logic_with_3_alu_bits_1_load_word),
    .ALU_OP_Code(kitchen_sink_control_logic_with_3_alu_bits_1_alu_op_code),
    .Jump(kitchen_sink_control_logic_with_3_alu_bits_1_jump),
    .Branch(kitchen_sink_control_logic_with_3_alu_bits_1_branch));
  // Probe on ram_1_data_2
  // Probe on kitchen_sink_control_logic_with_3_alu_bits_1_alu_op_code
  // Probe on ram_1_data[11:8]
  // Probe on ram_1_data[7:4]
  // Probe on ram_1_data[3:0]
  _16x16_bit_Register_File_with_Clear u_16x16_bit_register_file_with_clear_1 (
    .Data_In(CPU_Op_Out), .Write_Enable(kitchen_sink_control_logic_with_3_alu_bits_1_register_write_enable),
    .Clock(clock), .Clear(Clear), .Write_Address(ram_1_data[11:8]), .Read_Addr_1(ram_1_data[7:4]),
    .Read_Addr_2(ram_1_data[3:0]), .Read_Data_1(n16x16_bit_register_file_with_clear_1_read_data_1),
    .Read_Data_2(n16x16_bit_register_file_with_clear_1_read_data_2));
  Multiplexer #(.width(16), .enable("false")) multiplexer_3 (
    .in0(n16x16_bit_register_file_with_clear_1_read_data_2), .in1(bit_extender_1_out),
    .out(multiplexer_3_out), .sel(kitchen_sink_control_logic_with_3_alu_bits_1_immediate_select));
  assign bit_extender_1_out = {{12{ram_1_data[3]}}, ram_1_data[3:0]};  // Bit_Extender bit_extender_1
  assign bit_extender_2_out = {{13{ram_1_data[11]}}, ram_1_data[11:8]};  // Bit_Extender bit_extender_2
  _16_bit_CLA_ALU_with_Comparator u_16_bit_cla_alu_with_comparator_1 (
    .A(n16x16_bit_register_file_with_clear_1_read_data_1), .B(multiplexer_3_out),
    .ALU_Op(kitchen_sink_control_logic_with_3_alu_bits_1_alu_op_code), .ALU_Out(CPU_Op_Out),
    .Zero(n16_bit_cla_alu_with_comparator_1_zero));
  // Probe on ram_2_data
  Multiplexer #(.width(16), .enable("false")) multiplexer_4 (
    .in0(CPU_Op_Out), .in1(ram_2_data), .out(multiplexer_4_out),
    .sel(kitchen_sink_control_logic_with_3_alu_bits_1_load_word));
  or or_1 (or_1_out, kitchen_sink_control_logic_with_3_alu_bits_1_store_word, kitchen_sink_control_logic_with_3_alu_bits_1_load_word);
  RAM #(.addrWidth(16), .dataWidth(16), .bus("separate")) ram_2 (
    .addr(CPU_Op_Out), .din(multiplexer_4_out), .data(ram_2_data),
    .str(kitchen_sink_control_logic_with_3_alu_bits_1_store_word), .sel(or_1_out), .clk(clock),
    .ld(kitchen_sink_control_logic_with_3_alu_bits_1_load_word), .clr(Clear));

  // Notes on the sheet:
  //   branch
  //   op code
  //   branch
  //   src2
  //   immed data
  //   immed select
  //   ALU op
  //   dest
  //   src1
  //   jump
  //   store word
  //   load word
endmodule

module _16_bit_CLA_ALU_with_Comparator (
  input  [15:0] A,
  input  [15:0] B,
  input  [2:0] ALU_Op,
  output [15:0] ALU_Out,
  output Zero
);

  wire and_1_out, comparator_1_lt, comparator_2_gt;
  wire [15:0] and_2_out, bit_extender_1_out, bit_extender_2_out, multiplexer_1_out, n16_bit_cla_adder_1_s,
       not_1_out, or_1_out;

  assign not_1_out = ~B;  // NOT_Gate not_1, 16 bits wide
  Multiplexer #(.width(16), .enable("false")) multiplexer_1 (
    .in0(B), .in1(not_1_out), .out(multiplexer_1_out), .sel(and_1_out));
  and and_1 (and_1_out, ALU_Op[0], ALU_Op[1]);
  _16_bit_CLA_Adder u_16_bit_cla_adder_1 (
    .A(A), .B(multiplexer_1_out), .C_in(and_1_out), .S(n16_bit_cla_adder_1_s));  // open: C_out
  assign and_2_out = multiplexer_1_out & A;  // AND_Gate and_2, 16 bits wide
  assign or_1_out = multiplexer_1_out | A;  // OR_Gate or_1, 16 bits wide
  Comparator #(.width(16)) comparator_1 (.a(multiplexer_1_out), .b(A), .lt(comparator_1_lt));  // open: gt, eq
  assign bit_extender_1_out = {{15{comparator_1_lt}}, comparator_1_lt};  // Bit_Extender bit_extender_1
  assign bit_extender_2_out = {{15{comparator_2_gt}}, comparator_2_gt};  // Bit_Extender bit_extender_2
  Comparator #(.width(16)) comparator_2 (.a(multiplexer_1_out), .b(A), .gt(comparator_2_gt));  // open: eq, lt
  Multiplexer #(.select(3), .width(16), .enable("false")) multiplexer_2 (
    .in0(n16_bit_cla_adder_1_s), .in1(and_2_out), .in2(or_1_out), .in3(n16_bit_cla_adder_1_s),
    .in4(bit_extender_1_out), .in5(bit_extender_2_out), .out(ALU_Out), .sel(ALU_Op));  // open: in6, in7
  Comparator #(.width(16)) comparator_3 (.a(ALU_Out), .b({16{1'b0}}), .eq(Zero));  // open: gt, lt
  Pull_Resistor pull_resistor_1 (.node(Zero));

  // Notes on the sheet:
  //   Zero: pull=down
  //   000 = ADD
  //   001 = AND
  //   010 = OR
  //   011 = SUB
  //   100 = SLT
  //   101 = SGT
  //   sub not B
  //   sub cin
  //   sub
endmodule

module _16x16_bit_Register_File_with_Clear (
  input  [15:0] Data_In,
  input  Write_Enable,
  input  [3:0] Read_Addr_1,
  input  [3:0] Write_Address,
  input  [3:0] Read_Addr_2,
  input  Clock,
  input  Clear,
  output [15:0] Read_Data_1,
  output [15:0] Read_Data_2
);

  wire demultiplexer_1_out0, demultiplexer_1_out1, demultiplexer_1_out2, demultiplexer_1_out3,
       demultiplexer_1_out4, demultiplexer_1_out5, demultiplexer_1_out6, demultiplexer_1_out7,
       demultiplexer_1_out8, demultiplexer_1_out9, demultiplexer_1_out10, demultiplexer_1_out11,
       demultiplexer_1_out12, demultiplexer_1_out13, demultiplexer_1_out14, demultiplexer_1_out15;
  wire [15:0] register_1_q, register_2_q, register_3_q, register_4_q, register_5_q, register_6_q,
       register_7_q, register_8_q, register_9_q, register_10_q, register_11_q, register_12_q, register_13_q,
       register_14_q, register_15_q, register_16_q;

  Demultiplexer #(.select(4), .enable("false")) demultiplexer_1 (
    .out0(demultiplexer_1_out0), .out1(demultiplexer_1_out1), .out2(demultiplexer_1_out2),
    .out3(demultiplexer_1_out3), .out4(demultiplexer_1_out4), .out5(demultiplexer_1_out5),
    .out6(demultiplexer_1_out6), .out7(demultiplexer_1_out7), .out8(demultiplexer_1_out8),
    .out9(demultiplexer_1_out9), .out10(demultiplexer_1_out10), .out11(demultiplexer_1_out11),
    .out12(demultiplexer_1_out12), .out13(demultiplexer_1_out13), .out14(demultiplexer_1_out14),
    .out15(demultiplexer_1_out15), .in(Write_Enable), .sel(Write_Address));
  Register #(.width(16)) register_1 (
    .D(Data_In), .en(demultiplexer_1_out0), .Q(register_1_q), .clk(Clock), .clr(Clear));
  Register #(.width(16)) register_2 (
    .D(Data_In), .en(demultiplexer_1_out1), .Q(register_2_q), .clk(Clock), .clr(Clear));
  Register #(.width(16)) register_3 (
    .D(Data_In), .en(demultiplexer_1_out2), .Q(register_3_q), .clk(Clock), .clr(Clear));
  Register #(.width(16)) register_4 (
    .D(Data_In), .en(demultiplexer_1_out3), .Q(register_4_q), .clk(Clock), .clr(Clear));
  Register #(.width(16)) register_5 (
    .D(Data_In), .en(demultiplexer_1_out4), .Q(register_5_q), .clk(Clock), .clr(Clear));
  Register #(.width(16)) register_6 (
    .D(Data_In), .en(demultiplexer_1_out5), .Q(register_6_q), .clk(Clock), .clr(Clear));
  Register #(.width(16)) register_7 (
    .D(Data_In), .en(demultiplexer_1_out6), .Q(register_7_q), .clk(Clock), .clr(Clear));
  Register #(.width(16)) register_8 (
    .D(Data_In), .en(demultiplexer_1_out7), .Q(register_8_q), .clk(Clock), .clr(Clear));
  Register #(.width(16)) register_9 (
    .D(Data_In), .en(demultiplexer_1_out8), .Q(register_9_q), .clk(Clock), .clr(Clear));
  Register #(.width(16)) register_10 (
    .D(Data_In), .en(demultiplexer_1_out9), .Q(register_10_q), .clk(Clock), .clr(Clear));
  Register #(.width(16)) register_11 (
    .D(Data_In), .en(demultiplexer_1_out10), .Q(register_11_q), .clk(Clock), .clr(Clear));
  Register #(.width(16)) register_12 (
    .D(Data_In), .en(demultiplexer_1_out11), .Q(register_12_q), .clk(Clock), .clr(Clear));
  Register #(.width(16)) register_13 (
    .D(Data_In), .en(demultiplexer_1_out12), .Q(register_13_q), .clk(Clock), .clr(Clear));
  Register #(.width(16)) register_14 (
    .D(Data_In), .en(demultiplexer_1_out13), .Q(register_14_q), .clk(Clock), .clr(Clear));
  Register #(.width(16)) register_15 (
    .D(Data_In), .en(demultiplexer_1_out14), .Q(register_15_q), .clk(Clock), .clr(Clear));
  Register #(.width(16)) register_16 (
    .D(Data_In), .en(demultiplexer_1_out15), .Q(register_16_q), .clk(Clock), .clr(Clear));
  Multiplexer #(.select(4), .width(16), .enable("false")) multiplexer_1 (
    .in0(register_1_q), .in1(register_2_q), .in2(register_3_q), .in3(register_4_q), .in4(register_5_q),
    .in5(register_6_q), .in6(register_7_q), .in7(register_8_q), .in8(register_9_q), .in9(register_10_q),
    .in10(register_11_q), .in11(register_12_q), .in12(register_13_q), .in13(register_14_q),
    .in14(register_15_q), .in15(register_16_q), .out(Read_Data_1), .sel(Read_Addr_1));
  Multiplexer #(.select(4), .width(16), .enable("false")) multiplexer_2 (
    .in0(register_1_q), .in1(register_2_q), .in2(register_3_q), .in3(register_4_q), .in4(register_5_q),
    .in5(register_6_q), .in6(register_7_q), .in7(register_8_q), .in8(register_9_q), .in9(register_10_q),
    .in10(register_11_q), .in11(register_12_q), .in12(register_13_q), .in13(register_14_q),
    .in14(register_15_q), .in15(register_16_q), .out(Read_Data_2), .sel(Read_Addr_2));
endmodule

module Kitchen_Sink_Control_Logic_with_3_ALU_bits (
  input  [4:0] Opcode,
  output Register_Write_Enable,
  output Immediate_Select,
  output Store_Word,
  output Load_Word,
  output [2:0] ALU_OP_Code,
  output Jump,
  output Branch
);

  RAM #(.addrWidth(5), .dataWidth(9), .bus("separate")) ram_1 (
    .addr(Opcode),
    .data({Register_Write_Enable, Immediate_Select, Store_Word, Load_Word, ALU_OP_Code, Jump, Branch}),
    .ld(1'b1));  // open: din, str, sel, clk, clr
  // Probe on {Register_Write_Enable, Immediate_Select, Store_Word, Load_Word, ALU_OP_Code, Jump, Branch}

  // Notes on the sheet:
  //   Bit 1 is Jump
  //   Bit 0 is Branch
  //   Bit 7 is Register Enable
  //   Bit 6 is Immediate Select
  //   Bit 5 is Store Word
  //   Bit 4 is Load Word
  //   Bits 3 and 2 are ALU OP Code
endmodule
