// Logisim project Basic-Processor.circ as structural Verilog
module _16_bit_ALU (
  input  [15:0] A,
  input  [15:0] B,
  input  [1:0] ALU_Op,
  output [15:0] ALU_Out
);

  wire and_1_out;
  wire [15:0] adder_1_out, and_2_out, multiplexer_1_out, not_1_out, or_1_out;

  Multiplexer #(.width(16), .enable("false")) multiplexer_1 (
    .in0(B), .in1(not_1_out), .out(multiplexer_1_out), .sel(and_1_out));
  assign not_1_out = ~B;  // NOT_Gate not_1, 16 bits wide
  and and_1 (and_1_out, ALU_Op[0], ALU_Op[1]);
  Adder #(.width(16)) adder_1 (.a(A), .b(multiplexer_1_out), .out(adder_1_out), .cin(and_1_out));  // open: cout
  assign and_2_out = multiplexer_1_out & A;  // AND_Gate and_2, 16 bits wide
  assign or_1_out = multiplexer_1_out | A;  // OR_Gate or_1, 16 bits wide
  Multiplexer #(.select(2), .width(16), .enable("false")) multiplexer_2 (
    .in0(adder_1_out), .in1(and_2_out), .in2(or_1_out), .in3(adder_1_out), .out(ALU_Out), .sel(ALU_Op));

  // Notes on the sheet:
  //   00 = ADD
  //   01 = AND
  //   10 = OR
  //   11 = SUB
  //   sub not B
  //   sub cin
  //   sub
endmodule

module _16x16_bit_Register_File (
  input  [15:0] Data_In,
  input  Write_Enable,
  input  [3:0] Read_Addr_1,
  input  [3:0] Write_Address,
  input  [3:0] Read_Addr_2,
  input  Clock,
  output [15:0] Read_Data_1,
  output [15:0] Read_Data_2
);

  wire demultiplexer_1_out0, demultiplexer_1_out1, demultiplexer_1_out2, demultiplexer_1_out3,
       demultiplexer_1_out4, demultiplexer_1_out5, demultiplexer_1_out6, demultiplexer_1_out7,
       demultiplexer_1_out8, demultiplexer_1_out9, demultiplexer_1_out10, demultiplexer_1_out11,
       demultiplexer_1_out12, demultiplexer_1_out13, demultiplexer_1_out14, demultiplexer_1_out15;
  wire [15:0] register_1_q, register_2_q, register_3_q, register_4_q, register_5_q, register_6_q,
       register_7_q, register_8_q, register_9_q, register_10_q, register_11_q, register_12_q, register_13_q,
       register_14_q, register_15_q, register_16_q;

  Demultiplexer #(.select(4), .enable("false")) demultiplexer_1 (
    .out0(demultiplexer_1_out0), .out1(demultiplexer_1_out1), .out2(demultiplexer_1_out2),
    .out3(demultiplexer_1_out3), .out4(demultiplexer_1_out4), .out5(demultiplexer_1_out5),
    .out6(demultiplexer_1_out6), .out7(demultiplexer_1_out7), .out8(demultiplexer_1_out8),
    .out9(demultiplexer_1_out9), .out10(demultiplexer_1_out10), .out11(demultiplexer_1_out11),
    .out12(demultiplexer_1_out12), .out13(demultiplexer_1_out13), .out14(demultiplexer_1_out14),
    .out15(demultiplexer_1_out15), .in(Write_Enable), .sel(Write_Address));
  Register #(.width(16)) register_1 (
    .D(Data_In), .en(demultiplexer_1_out0), .Q(register_1_q), .clk(Clock));  // open: clr
  Register #(.width(16)) register_2 (
    .D(Data_In), .en(demultiplexer_1_out1), .Q(register_2_q), .clk(Clock));  // open: clr
  Register #(.width(16)) register_3 (
    .D(Data_In), .en(demultiplexer_1_out2), .Q(register_3_q), .clk(Clock));  // open: clr
  Register #(.width(16)) register_4 (
    .D(Data_In), .en(demultiplexer_1_out3), .Q(register_4_q), .clk(Clock));  // open: clr
  Register #(.width(16)) register_5 (
    .D(Data_In), .en(demultiplexer_1_out4), .Q(register_5_q), .clk(Clock));  // open: clr
  Register #(.width(16)) register_6 (
    .D(Data_In), .en(demultiplexer_1_out5), .Q(register_6_q), .clk(Clock));  // open: clr
  Register #(.width(16)) register_7 (
    .D(Data_In), .en(demultiplexer_1_out6), .Q(register_7_q), .clk(Clock));  // open: clr
  Register #(.width(16)) register_8 (
    .D(Data_In), .en(demultiplexer_1_out7), .Q(register_8_q), .clk(Clock));  // open: clr
  Register #(.width(16)) register_9 (
    .D(Data_In), .en(demultiplexer_1_out8), .Q(register_9_q), .clk(Clock));  // open: clr
  Register #(.width(16)) register_10 (
    .D(Data_In), .en(demultiplexer_1_out9), .Q(register_10_q), .clk(Clock));  // open: clr
  Register #(.width(16)) register_11 (
    .D(Data_In), .en(demultiplexer_1_out10), .Q(register_11_q), .clk(Clock));  // open: clr
  Register #(.width(16)) register_12 (
    .D(Data_In), .en(demultiplexer_1_out11), .Q(register_12_q), .clk(Clock));  // open: clr
  Register #(.width(16)) register_13 (
    .D(Data_In), .en(demultiplexer_1_out12), .Q(register_13_q), .clk(Clock));  // open: clr
  Register #(.width(16)) register_14 (
    .D(Data_In), .en(demultiplexer_1_out13), .Q(register_14_q), .clk(Clock));  // open: clr
  Register #(.width(16)) register_15 (
    .D(Data_In), .en(demultiplexer_1_out14), .Q(register_15_q), .clk(Clock));  // open: clr
  Register #(.width(16)) register_16 (
    .D(Data_In), .en(demultiplexer_1_out15), .Q(register_16_q), .clk(Clock));  // open: clr
  Multiplexer #(.select(4), .width(16), .enable("false")) multiplexer_1 (
    .in0(register_1_q), .in1(register_2_q), .in2(register_3_q), .in3(register_4_q), .in4(register_5_q),
    .in5(register_6_q), .in6(register_7_q), .in7(register_8_q), .in8(register_9_q), .in9(register_10_q),
    .in10(register_11_q), .in11(register_12_q), .in12(register_13_q), .in13(register_14_q),
    .in14(register_15_q), .in15(register_16_q), .out(Read_Data_1), .sel(Read_Addr_1));
  Multiplexer #(.select(4), .width(16), .enable("false")) multiplexer_2 (
    .in0(register_1_q), .in1(register_2_q), .in2(register_3_q), .in3(register_4_q), .in4(register_5_q),
    .in5(register_6_q), .in6(register_7_q), .in7(register_8_q), .in8(register_9_q), .in9(register_10_q),
    .in10(register_11_q), .in11(register_12_q), .in12(register_13_q), .in13(register_14_q),
    .in14(register_15_q), .in15(register_16_q), .out(Read_Data_2), .sel(Read_Addr_2));
endmodule

module _16_bit_ALU_REG_Instruction (
  input  [16:0] CPU_Instruction_Input,
  input  clock,
  output [15:0] CPU_Op_Out
);

  wire [15:0] bit_extender_1_out, multiplexer_1_out, n16x16_bit_register_file_1_read_data_1,
       n16x16_bit_register_file_1_read_data_2;

  _16x16_bit_Register_File u_16x16_bit_register_file_1 (
    .Data_In(CPU_Op_Out), .Write_Enable(1'b1), .Clock(clock), .Write_Address(CPU_Instruction_Input[8:5]),
    .Read_Addr_1(CPU_Instruction_Input[12:9]), .Read_Addr_2(CPU_Instruction_Input[16:13]),
    .Read_Data_1(n16x16_bit_register_file_1_read_data_1), .Read_Data_2(n16x16_bit_register_file_1_read_data_2));
  assign bit_extender_1_out = {{12{CPU_Instruction_Input[16]}}, CPU_Instruction_Input[16:13]};  // Bit_Extender bit_extender_1
  Multiplexer #(.width(16), .enable("false")) multiplexer_1 (
    .in0(n16x16_bit_register_file_1_read_data_2), .in1(bit_extender_1_out), .out(multiplexer_1_out),
    .sel(CPU_Instruction_Input[4]));
  _16_bit_ALU u_16_bit_alu_1 (
    .A(n16x16_bit_register_file_1_read_data_1), .B(multiplexer_1_out), .ALU_Op(CPU_Instruction_Input[1:0]),
    .ALU_Out(CPU_Op_Out));

  // Notes on the sheet:
  //   op code
  //   src2
  //   ALU op
  //   dest
  //   src1
  //   immed data
  //   immed select
endmodule

module _16_bit_ALU_with_Memory (
  input  [16:0] CPU_Instruction_Input,
  input  clock,
  output [15:0] CPU_Op_Out
);

  wire control_logic_lookup_table_1_immediate_select, control_logic_lookup_table_1_load_word,
       control_logic_lookup_table_1_register_write_enable, control_logic_lookup_table_1_store_word, or_1_out;
  wire [1:0] control_logic_lookup_table_1_alu_op_code;
  wire [15:0] bit_extender_1_out, multiplexer_1_out, multiplexer_2_out,
       n16x16_bit_register_file_1_read_data_1, n16x16_bit_register_file_1_read_data_2, ram_1_data;

  Control_Logic_Lookup_Table control_logic_lookup_table_1 (
    .Opcode(CPU_Instruction_Input[4:0]),
    .Register_Write_Enable(control_logic_lookup_table_1_register_write_enable),
    .Immediate_Select(control_logic_lookup_table_1_immediate_select),
    .Store_Word(control_logic_lookup_table_1_store_word), .Load_Word(control_logic_lookup_table_1_load_word),
    .ALU_OP_Code(control_logic_lookup_table_1_alu_op_code));
  assign bit_extender_1_out = {{12{CPU_Instruction_Input[16]}}, CPU_Instruction_Input[16:13]};  // Bit_Extender bit_extender_1
  _16x16_bit_Register_File u_16x16_bit_register_file_1 (
    .Data_In(CPU_Op_Out), .Write_Enable(control_logic_lookup_table_1_register_write_enable), .Clock(clock),
    .Write_Address(CPU_Instruction_Input[8:5]), .Read_Addr_1(CPU_Instruction_Input[12:9]),
    .Read_Addr_2(CPU_Instruction_Input[16:13]), .Read_Data_1(n16x16_bit_register_file_1_read_data_1),
    .Read_Data_2(n16x16_bit_register_file_1_read_data_2));
  Multiplexer #(.width(16), .enable("false")) multiplexer_1 (
    .in0(n16x16_bit_register_file_1_read_data_2), .in1(bit_extender_1_out), .out(multiplexer_1_out),
    .sel(control_logic_lookup_table_1_immediate_select));
  _16_bit_ALU u_16_bit_alu_1 (
    .A(n16x16_bit_register_file_1_read_data_1), .B(multiplexer_1_out),
    .ALU_Op(control_logic_lookup_table_1_alu_op_code), .ALU_Out(CPU_Op_Out));
  Multiplexer #(.width(16), .enable("false")) multiplexer_2 (
    .in0(ram_1_data), .in1(CPU_Op_Out), .out(multiplexer_2_out), .sel(control_logic_lookup_table_1_load_word));
  or or_1 (or_1_out, control_logic_lookup_table_1_store_word, control_logic_lookup_table_1_load_word);
  RAM #(.addrWidth(16), .dataWidth(16), .bus("separate")) ram_1 (
    .addr(CPU_Op_Out), .din(multiplexer_2_out), .data(ram_1_data),
    .str(control_logic_lookup_table_1_store_word), .sel(or_1_out), .clk(clock),
    .ld(control_logic_lookup_table_1_load_word));  // open: clr

  // Notes on the sheet:
  //   op code
  //   src1
  //   src2
  //   immed data
  //   immed select
  //   ALU op
  //   dest
endmodule

module Control_Logic_Lookup_Table (
  input  [4:0] Opcode,
  output Register_Write_Enable,
  output Immediate_Select,
  output Store_Word,
  output Load_Word,
  output [1:0] ALU_OP_Code
);

  wire [1:0] ram_1_data;

  RAM #(.addrWidth(5), .bus("separate")) ram_1 (
    .addr(Opcode),
    .data({Register_Write_Enable, Immediate_Select, Store_Word, Load_Word, ALU_OP_Code, ram_1_data}),
    .ld(1'b1));  // open: din, str, sel, clk, clr
  // Probe on {Register_Write_Enable, Immediate_Select, Store_Word, Load_Word, ALU_OP_Code, ram_1_data}

  // Notes on the sheet:
  //   Bit 2 is Store Word
  //   Bit 3 is Load Word
  //   Bit 0 is Register Write Enable
  //   Bit 1 is Immediate Select
  //   Bits 4 and 5 are ALU OP Code
endmodule

module Full_16_bit_CPU (
  input  clock
);

  wire control_logic_lookup_table_1_immediate_select, control_logic_lookup_table_1_load_word,
       control_logic_lookup_table_1_register_write_enable, control_logic_lookup_table_1_store_word, or_1_out;
  wire [1:0] control_logic_lookup_table_1_alu_op_code;
  wire [15:0] bit_extender_1_out, multiplexer_1_out, multiplexer_2_out, n16_bit_alu_1_alu_out,
       n16x16_bit_register_file_1_read_data_1, n16x16_bit_register_file_1_read_data_2, ram_2_data;
  wire [16:0] adder_1_out, ram_1_data, register_1_q;

  Adder #(.width(17)) adder_1 (.a(17'h1), .b(register_1_q), .out(adder_1_out));  // open: cin, cout
  Register #(.width(17)) register_1 (.D(adder_1_out), .Q(register_1_q), .clk(clock));  // open: en, clr
  RAM #(.addrWidth(17), .dataWidth(17), .bus("separate")) ram_1 (
    .addr(register_1_q), .data(ram_1_data), .clk(clock));  // open: din, str, sel, ld, clr
  Control_Logic_Lookup_Table control_logic_lookup_table_1 (
    .Opcode(ram_1_data[16:12]), .Register_Write_Enable(control_logic_lookup_table_1_register_write_enable),
    .Immediate_Select(control_logic_lookup_table_1_immediate_select),
    .Store_Word(control_logic_lookup_table_1_store_word), .Load_Word(control_logic_lookup_table_1_load_word),
    .ALU_OP_Code(control_logic_lookup_table_1_alu_op_code));
  _16x16_bit_Register_File u_16x16_bit_register_file_1 (
    .Data_In(n16_bit_alu_1_alu_out), .Write_Enable(control_logic_lookup_table_1_register_write_enable),
    .Clock(clock), .Write_Address(ram_1_data[11:8]), .Read_Addr_1(ram_1_data[7:4]),
    .Read_Addr_2(ram_1_data[3:0]), .Read_Data_1(n16x16_bit_register_file_1_read_data_1),
    .Read_Data_2(n16x16_bit_register_file_1_read_data_2));
  assign bit_extender_1_out = {{12{ram_1_data[3]}}, ram_1_data[3:0]};  // Bit_Extender bit_extender_1
  _16_bit_ALU u_16_bit_alu_1 (
    .A(n16x16_bit_register_file_1_read_data_1), .B(multiplexer_1_out),
    .ALU_Op(control_logic_lookup_table_1_alu_op_code), .ALU_Out(n16_bit_alu_1_alu_out));
  Multiplexer #(.width(16), .enable("false")) multiplexer_1 (
    .in0(n16x16_bit_register_file_1_read_data_2), .in1(bit_extender_1_out), .out(multiplexer_1_out),
    .sel(control_logic_lookup_table_1_immediate_select));
  Multiplexer #(.width(16), .enable("false")) multiplexer_2 (
    .in0(n16_bit_alu_1_alu_out), .in1(ram_2_data), .out(multiplexer_2_out),
    .sel(control_logic_lookup_table_1_load_word));
  or or_1 (or_1_out, control_logic_lookup_table_1_store_word, control_logic_lookup_table_1_load_word);
  RAM #(.addrWidth(16), .dataWidth(16), .bus("separate")) ram_2 (
    .addr(n16_bit_alu_1_alu_out), .din(multiplexer_2_out), .data(ram_2_data),
    .str(control_logic_lookup_table_1_store_word), .sel(or_1_out), .clk(clock),
    .ld(control_logic_lookup_table_1_load_word));  // open: clr

  // Notes on the sheet:
  //   op code
  //   src2
  //   src1
  //   immed data
  //   immed select
  //   ALU op
  //   dest
endmodule
